# Fritzing sketch li_ion_cell_discharger (saved by Fritzing 0.9.3b)
breadboards: 1

parts:
  Part1 = Arduino Nano (Rev3.0)
  R5 = Resistor [tolerance=±5% resistance=1 package=THT]
  V2 = DC Power [voltage=5]
  Q3 = MOSFET-NCHANNEL [package=to220v]
  R7 = Resistor [tolerance=±5% resistance=10k package="0402 [SMD]"]
  R2 = Resistor [tolerance=±5% resistance=3.3 package=THT]
  Q4 = MOSFET-NCHANNEL [package=to220v]
  R8 = Resistor [tolerance=±5% resistance=10k package="0402 [SMD]"]
  R9 = Resistor [tolerance=±5% resistance=3.3 package=THT]
  R10 = Resistor [tolerance=±5% resistance=1 package=THT]
  V3 = DC Power [voltage=5]
  LED1 = smd LED [color="Red (633nm)" package="1206 [SMD]"]
  R11 = Resistor [tolerance=±5% resistance=1k package="0402 [SMD]"]
  LED2 = smd LED [color="Red (633nm)" package="1206 [SMD]"]
  R12 = Resistor [tolerance=±5% resistance=1k package="0402 [SMD]"]
  S1 = Momentary Switch [package=ksa_sealed_tac_switch]
  S2 = Momentary Switch [package=ksa_sealed_tac_switch]

nets:
  GND: Part1.GND, V2.V-, Q3.S, R7.Pin_0, Q4.S, R8.Pin_0, V3.V-, LED1.cathode, LED2.cathode, S1.3, S2.4
  N1: Part1.D6, S2.2
  N2: Part1.D7, S1.2
  N3: Part1.D12/MISO, R12.Pin_0
  N4: Part1.A3, R9.Pin_1, R10.Pin_0
  N5: Part1.A2, R10.Pin_1, V3.V+
  N6: Part1.A1, R5.Pin_0, R2.Pin_1
  N7: Part1.A0, R5.Pin_1, V2.V+
  N8: Part1.D13/SCK, R11.Pin_0
  N9: Q3.G, R7.Pin_1
  N10: Q3.D, R2.Pin_0
  N11: Q4.G, R8.Pin_1
  N12: Q4.D, R9.Pin_0
  N13: LED1.anode, R11.Pin_1
  N14: LED2.anode, R12.Pin_1
